// Digital circuit MaquinaDeEscrever.dig as structural Verilog
module MaquinaDeEscrever (
  input  in_1,
  input  clk,
  input  in_3,
  input  in_4,
  input  in_5,
  input  in_6,
  input  in_7
);

  wire button_1_out, button_2_out, button_3_out, button_4_out, u_impressora_hex00, u_impressora_hex01,
       u_impressora_hex02, u_impressora_hex03, u_impressora_hex04, u_impressora_hex05, u_impressora_hex06,
       u_impressora_hex10, u_impressora_hex11, u_impressora_hex12, u_impressora_hex13, u_impressora_hex14,
       u_impressora_hex15, u_impressora_hex16, u_impressora_hex20, u_impressora_hex21, u_impressora_hex22,
       u_impressora_hex23, u_impressora_hex24, u_impressora_hex25, u_impressora_hex26, u_impressora_hex30,
       u_impressora_hex31, u_impressora_hex32, u_impressora_hex33, u_impressora_hex34, u_impressora_hex35,
       u_impressora_hex36;

  Button button_1 (.out(button_1_out));
  Button button_2 (.out(button_2_out));
  Button button_3 (.out(button_3_out));
  Button button_4 (.out(button_4_out));
  impressora #(.applicationType("GHDL"), .CodeFile("C:\\Users\\User\\Desktop\\faculdade_cc\\3semestre\\sistemasDigitais\\vhdl\\trabalho final\\impressora.vhd")) u_impressora (
    .clock(clk), .sw4(in_3), .sw3(in_4), .sw2(in_5), .sw1(in_6), .sw0(in_7), .mudarLetra(button_1_out),
    .mudarPos(button_2_out), .reset(button_3_out), .gravar(button_4_out), .hex00(u_impressora_hex00),
    .hex01(u_impressora_hex01), .hex02(u_impressora_hex02), .hex03(u_impressora_hex03),
    .hex04(u_impressora_hex04), .hex05(u_impressora_hex05), .hex06(u_impressora_hex06),
    .hex10(u_impressora_hex10), .hex11(u_impressora_hex11), .hex12(u_impressora_hex12),
    .hex13(u_impressora_hex13), .hex14(u_impressora_hex14), .hex15(u_impressora_hex15),
    .hex16(u_impressora_hex16), .hex20(u_impressora_hex20), .hex21(u_impressora_hex21),
    .hex22(u_impressora_hex22), .hex23(u_impressora_hex23), .hex24(u_impressora_hex24),
    .hex25(u_impressora_hex25), .hex26(u_impressora_hex26), .hex30(u_impressora_hex30),
    .hex31(u_impressora_hex31), .hex32(u_impressora_hex32), .hex33(u_impressora_hex33),
    .hex34(u_impressora_hex34), .hex35(u_impressora_hex35), .hex36(u_impressora_hex36));
  Seven_Seg #(.commonCathode("true"), .commonConnectionType("anode")) seven_seg_1 (
    .a(u_impressora_hex00), .b(u_impressora_hex01), .c(u_impressora_hex02), .d(u_impressora_hex03),
    .e(u_impressora_hex04), .f(u_impressora_hex05), .g(u_impressora_hex06), .dp(in_1), .common(in_1));
  Seven_Seg #(.commonConnectionType("anode"), .commonCathode("true")) seven_seg_2 (
    .a(u_impressora_hex10), .b(u_impressora_hex11), .c(u_impressora_hex12), .d(u_impressora_hex13),
    .e(u_impressora_hex14), .f(u_impressora_hex15), .g(u_impressora_hex16), .dp(in_1), .common(in_1));
  Seven_Seg #(.commonCathode("true"), .commonConnectionType("anode")) seven_seg_3 (
    .a(u_impressora_hex20), .b(u_impressora_hex21), .c(u_impressora_hex22), .d(u_impressora_hex23),
    .e(u_impressora_hex24), .f(u_impressora_hex25), .g(u_impressora_hex26), .dp(in_1), .common(in_1));
  Seven_Seg #(.commonCathode("true"), .commonConnectionType("anode")) seven_seg_4 (
    .a(u_impressora_hex30), .b(u_impressora_hex31), .c(u_impressora_hex32), .d(u_impressora_hex33),
    .e(u_impressora_hex34), .f(u_impressora_hex35), .g(u_impressora_hex36), .dp(in_1), .common(in_1));

  // Notes on the sheet:
  //   in_1: default 1
endmodule
