// Digital circuit MaquinaDeLer.dig as structural Verilog
module MaquinaDeLer (
  input  in_1,
  input  [4:0] in_2,
  input  [4:0] in_3,
  input  [4:0] in_4,
  input  [4:0] in_5,
  input  clk,
  input  [4:0] in_7,
  input  [4:0] in_8,
  input  [4:0] in_9,
  input  [4:0] in_10,
  input  [4:0] in_11,
  input  [4:0] in_12
);

  wire button_1_out, u_ler_hex00, u_ler_hex01, u_ler_hex02, u_ler_hex03, u_ler_hex04, u_ler_hex05,
       u_ler_hex06, u_ler_hex10, u_ler_hex11, u_ler_hex12, u_ler_hex13, u_ler_hex14, u_ler_hex15,
       u_ler_hex16, u_ler_hex20, u_ler_hex21, u_ler_hex22, u_ler_hex23, u_ler_hex24, u_ler_hex25,
       u_ler_hex26, u_ler_hex30, u_ler_hex31, u_ler_hex32, u_ler_hex33, u_ler_hex34, u_ler_hex35, u_ler_hex36;

  Button button_1 (.out(button_1_out));
  ler #(.applicationType("GHDL"), .CodeFile("C:\\Users\\User\\Desktop\\faculdade_cc\\3semestre\\sistemasDigitais\\vhdl\\trabalho final\\escrever.vhd")) u_ler (
    .clock(clk), .reset(button_1_out), .p0(in_2), .p1(in_3), .p2(in_4), .p3(in_5), .p4(in_7), .p5(in_8),
    .p6(in_9), .p7(in_10), .p8(in_11), .p9(in_12), .hex00(u_ler_hex00), .hex01(u_ler_hex01),
    .hex02(u_ler_hex02), .hex03(u_ler_hex03), .hex04(u_ler_hex04), .hex05(u_ler_hex05), .hex06(u_ler_hex06),
    .hex10(u_ler_hex10), .hex11(u_ler_hex11), .hex12(u_ler_hex12), .hex13(u_ler_hex13), .hex14(u_ler_hex14),
    .hex15(u_ler_hex15), .hex16(u_ler_hex16), .hex20(u_ler_hex20), .hex21(u_ler_hex21), .hex22(u_ler_hex22),
    .hex23(u_ler_hex23), .hex24(u_ler_hex24), .hex25(u_ler_hex25), .hex26(u_ler_hex26), .hex30(u_ler_hex30),
    .hex31(u_ler_hex31), .hex32(u_ler_hex32), .hex33(u_ler_hex33), .hex34(u_ler_hex34), .hex35(u_ler_hex35),
    .hex36(u_ler_hex36));
  Seven_Seg #(.commonCathode("true"), .commonConnectionType("anode")) seven_seg_1 (
    .a(u_ler_hex00), .b(u_ler_hex01), .c(u_ler_hex02), .d(u_ler_hex03), .e(u_ler_hex04), .f(u_ler_hex05),
    .g(u_ler_hex06), .dp(in_1), .common(in_1));
  Seven_Seg #(.commonCathode("true"), .commonConnectionType("anode")) seven_seg_2 (
    .a(u_ler_hex10), .b(u_ler_hex11), .c(u_ler_hex12), .d(u_ler_hex13), .e(u_ler_hex14), .f(u_ler_hex15),
    .g(u_ler_hex16), .dp(in_1), .common(in_1));
  Seven_Seg #(.commonCathode("true"), .commonConnectionType("anode")) seven_seg_3 (
    .a(u_ler_hex20), .b(u_ler_hex21), .c(u_ler_hex22), .d(u_ler_hex23), .e(u_ler_hex24), .f(u_ler_hex25),
    .g(u_ler_hex26), .dp(in_1), .common(in_1));
  Seven_Seg #(.commonCathode("true"), .commonConnectionType("anode")) seven_seg_4 (
    .a(u_ler_hex30), .b(u_ler_hex31), .c(u_ler_hex32), .d(u_ler_hex33), .e(u_ler_hex34), .f(u_ler_hex35),
    .g(u_ler_hex36), .dp(in_1), .common(in_1));

  // Notes on the sheet:
  //   in_1: default 1
endmodule
