// Digital circuit teat.dig as structural Verilog
module teat (
  input  in_1,
  input  in_2,
  input  [4:0] in_3,
  input  [4:0] in_4,
  input  [4:0] in_5,
  input  [4:0] in_6,
  input  [4:0] in_7,
  input  [4:0] in_8,
  input  [4:0] in_9,
  input  [4:0] in_10,
  input  [4:0] in_11,
  input  [4:0] in_12,
  output out_13,
  output out_14,
  output out_15,
  output out_16,
  output out_17,
  output out_18,
  output out_19,
  output out_20,
  output out_21,
  output out_22,
  output out_23,
  output out_24,
  output out_25,
  output out_26,
  output out_27,
  output out_28,
  output out_29,
  output out_30,
  output out_31,
  output out_32,
  output out_33
);

  ent #(.applicationType("GHDL"), .CodeFile("C:\\Users\\User\\Desktop\\faculdade_cc\\3semestre\\sistemasDigitais\\vhdl\\trabalho final\\test.vhd")) u_ent (
    .clock(in_1), .reset(in_2), .p0(in_3), .p1(in_4), .p2(in_5), .p3(in_6), .p4(in_7), .p5(in_8), .p6(in_9),
    .p7(in_10), .p8(in_11), .p9(in_12), .hex00(out_13), .hex01(out_14), .hex02(out_15), .hex03(out_16),
    .hex04(out_17), .hex05(out_18), .hex06(out_19), .hex10(out_20), .hex11(out_21), .hex12(out_22),
    .hex13(out_23), .hex14(out_24), .hex15(out_25), .hex16(out_26), .hex20(out_27), .hex21(out_28),
    .hex22(out_29), .hex23(out_30), .hex24(out_31), .hex25(out_32), .hex26(out_33));  // open: hex30, hex31, hex32, hex33, hex34, hex35, hex36
endmodule
